// Logisim project universal_cs23b1051.circ as structural Verilog: 1 circuit, main circuit main
module main (
  input  I0,
  input  I3,
  input  I2,
  input  I1,
  input  LS,
  input  RS,
  input  [1:0] in_7,
  input  in_8,
  output A0,
  output A3,
  output A2,
  output A1
);

  wire clock_1_out, multiplexer_1_out, multiplexer_2_out, multiplexer_3_out, multiplexer_4_out;

  Clock clock_1 (.out(clock_1_out));
  D_Flip_Flop d_ff_1 (.D(multiplexer_1_out), .clk(clock_1_out), .Q(A3), .reset(in_8));  // open: Qn, preset
  Multiplexer #(.select(2)) multiplexer_1 (.in0(A3), .in1(RS), .in2(A2), .in3(I3), .out(multiplexer_1_out), .sel(in_7));
  Multiplexer #(.select(2)) multiplexer_2 (.in0(A2), .in1(A3), .in2(A1), .in3(I2), .out(multiplexer_2_out), .sel(in_7));
  D_Flip_Flop d_ff_2 (.D(multiplexer_2_out), .clk(clock_1_out), .Q(A2), .reset(in_8));  // open: Qn, preset
  Multiplexer #(.select(2)) multiplexer_3 (.in0(A1), .in1(A2), .in2(A0), .in3(I1), .out(multiplexer_3_out), .sel(in_7));
  D_Flip_Flop d_ff_3 (.D(multiplexer_3_out), .clk(clock_1_out), .Q(A1), .reset(in_8));  // open: Qn, preset
  Multiplexer #(.select(2)) multiplexer_4 (.in0(A0), .in1(A1), .in2(LS), .in3(I0), .out(multiplexer_4_out), .sel(in_7));
  D_Flip_Flop d_ff_4 (.D(multiplexer_4_out), .clk(clock_1_out), .Q(A0), .reset(in_8));  // open: Qn, preset
endmodule
